# Fritzing sketch schema (saved by Fritzing 0.9.3b)
breadboards: 1

parts:
  LED1 = RGB LED (com. cathode, rgb) [package="5 mm [THT]"]
  LED2 = RGB LED (com. cathode, rgb) [package="5 mm [THT]"]
  S2 = Pushbutton [package="[THT]"]
  LED3 = RGB LED (com. cathode, rgb) [package="5 mm [THT]"]
  LED4 = RGB LED (com. cathode, rgb) [package="5 mm [THT]"]
  S3 = Pushbutton [package="[THT]"]
  S4 = Pushbutton [package="[THT]"]
  S5 = Pushbutton [package="[THT]"]
  Part1 = Arduino Mega 2560 (Rev3)

nets:
  N1: LED1.common_cathode, LED2.common_cathode, S2.Pin_1, S2.Pin_2, LED3.common_cathode, LED4.common_cathode, S3.Pin_1, S3.Pin_2, S4.Pin_1, S4.Pin_2, S5.Pin_1, S5.Pin_2, Part1.GND
  N2: LED1.green_anode, LED2.green_anode, LED3.green_anode, LED4.green_anode, Part1.5V
  N3: LED1.blue_anode, LED2.red_anode
  N4: LED2.blue_anode, LED4.red_anode
  N5: S2.Pin_3, S2.Pin_4, Part1.D50
  N6: LED3.red_anode, LED4.blue_anode
  N7: LED3.blue_anode, Part1.D2_PWM
  N8: S3.Pin_3, S3.Pin_4, Part1.D51
  N9: S4.Pin_3, S4.Pin_4, Part1.D52
  N10: S5.Pin_3, S5.Pin_4, Part1.D53
